# Fritzing sketch led_blink_schematic (saved by Fritzing 0.9.3b)
breadboards: 1

parts:
  Part1 = Arduino Uno (Rev3)
  LED1 = LED - 5mm [color="Red (633nm)" package="5 mm [THT]"]
  R1 = Resistor [tolerance=±5% resistance=220 package="0402 [SMD]"]

nets:
  N1: Part1.D9_PWM, R1.Pin_0
  N2: Part1.GND, LED1.anode
  N3: LED1.cathode, R1.Pin_1
