# Fritzing sketch pot_servo_schematic (saved by Fritzing 0.9.3b)
breadboards: 1

parts:
  R1 = Rotary Potentiometer (Small) [maximum_resistance=100kΩ package=THT]
  Part1 = Arduino Uno (Rev3)
  YwRobot_Power_Supply1 = YwRobot Breadboard Power Supply [part_number=545043]
  J1 = Basic Servo

nets:
  N1: R1.leg1, Part1.GND, YwRobot_Power_Supply1.GND#13
  N2: R1.wiper, Part1.A0
  N3: R1.leg2, Part1.5V, YwRobot_Power_Supply1.VCC#9
  N4: YwRobot_Power_Supply1.VCC#5, J1.vcc
  N5: YwRobot_Power_Supply1.GND#11, J1.gnd

custom parts:
  YwRobot Breadboard Power Supply: The YwRobot Breadboard Power Supply (MB-V2) has two power rails; they can be 5V or 3V3. Power to the module can be provided through the female USB socket or through the A10 (female) 2.1mm power jack.
